# Fritzing sketch Rtc_Ultrasonic_DHT11 (saved by Fritzing 0.9.1b)
breadboards: 1

parts:
  Composant1 = Arduino Nano (Rev3.0)
  Composant2 = Real Time Clock Module - DS1307 RTC Breakout Board
  R1 = PHOTOCELL [package=photocell-kit]
  DHT2 = DHT11 Humitidy and Temperature Sensor
  Part4 = SRF05 Ultrasonic Rangefinder
  R2 = Resistor [tolerance=±5% resistance=220 package=THT]
  J1 = Screw terminal - 2 pins [package=THT]

nets:
  GND: Composant1.GND, Composant2.GND, DHT2.GND, Part4.GND, R2.Pin_1, J1.pin2
  N1: Composant1.D11/MOSI, Part4.Echo
  N2: Composant1.D12/MISO, Part4.Trig
  5V: Composant1.5V, Composant2.5V, R1.P$2, DHT2.NULL, Part4.VCC
  N3: Composant1.A5, Composant2.SCL
  N4: Composant1.A4, Composant2.SDA
  N5: Composant1.A3, J1.pin1
  N6: Composant1.A2, R1.P$1, R2.Pin_0
  N7: Composant1.A0, DHT2.DATA

notes:
  To water

custom parts:
  DHT11 Humitidy and Temperature Sensor: DHT11 Humidity and Temperature Sensor

// code stored in the sketch: Rtc_UltraSonic_DHT11.ino
/* 
* Rtc_UltraSonic_DHT11
* https://github.com/Jodaille/joduino/tree/master/arduino/sketchbook/Rtc_UltraSonic_DHT11
* Clock
* cf:
* https://learn.adafruit.com/ds1307-real-time-clock-breakout-board-kit/understanding-the-code
*/
#include <Wire.h>
#include "RTClib.h" 
RTC_DS1307 RTC;

// Ultrasonic sensor
#include <NewPing.h>
#define TRIGGER_PIN  12
#define ECHO_PIN     11
#define MAX_DISTANCE 200 
NewPing sonar(TRIGGER_PIN, ECHO_PIN, MAX_DISTANCE);

// DHT11 sensor
#include <dht11.h>
dht11 DHT11;
#define DHT11PIN A0

/* Low level detection
cf: http://bateaux.trucs.free.fr/detecteur_eau_sans_composant.html
*/
const int lowlevel = A3;

int lightPin = A2;

// Warning led
const int warning = 13;

// read interval management
long previousMillis = 0;        // will store last time data was updated

// the follow variables is a long because the time, measured in miliseconds,
// will quickly become a bigger number than can be stored in an int.
long interval = 1000;           // interval at which to process (milliseconds)

void setup() {

    Serial.begin(9600);

    Wire.begin();
    RTC.begin();

    if (! RTC.isrunning()) {
        Serial.println("RTC is NOT running!");
        // following line sets the RTC to the date & time this sketch was compiled
        //RTC.adjust(DateTime(__DATE__, __TIME__));
    }

    // low water level
    pinMode(lowlevel, INPUT); 
    
}
 
void loop() {

    unsigned long currentMillis = millis();
 
    if(currentMillis - previousMillis > interval) {
        // save the last time we read data 
        previousMillis = currentMillis;

        int light = analogRead(lightPin);

        // Sonar distance
        int uS = sonar.ping();
        
        // Time
        DateTime now = RTC.now();
        
        // Temperature and humidity
        int chk = DHT11.read(DHT11PIN);
        
        // Display result
        Serial.print("{'date':'");
        Serial.print(now.year(),DEC);
        Serial.print('-');
        printDigits(now.month());
        Serial.print('-');
        printDigits(now.day());
        Serial.print('T');
        printDigits(now.hour());
        Serial.print(':');
        printDigits(now.minute());
        Serial.print(':');
        printDigits(now.second());
        Serial.print("',");
        Serial.print("'waterlevel':");
        Serial.print(uS / US_ROUNDTRIP_CM);
        Serial.print(",");

        Serial.print("'light':");
        Serial.print(light);
        Serial.print(",");

        Serial.print("'humidity':'");
        Serial.print((float)DHT11.humidity, 2);
        Serial.print("',");

        Serial.print("'temperature':");
        Serial.print((float)DHT11.temperature, 2);
        
        // Low level alert 
        Serial.print("'alarm':");
        digitalWrite(lowlevel, HIGH); // enable internal pull-up
        if (digitalRead(lowlevel))
        {
            //Serial.println("!!! MISSING WATER !!!");
            Serial.print("'low water level'");
            digitalWrite(warning, HIGH);
        }
        else
        {
            Serial.print("''");
            digitalWrite(warning, LOW);
        }
        digitalWrite(lowlevel, LOW); // disable internal pull-up

        Serial.println("}");        
        
    }
}

void printDigits(byte digits){
  // utility function for digital clock display: prints colon and leading 0
  if(digits < 10)
    Serial.print('0');
  Serial.print(digits,DEC);   
}
